# Fritzing sketch schematic (saved by Fritzing 0.9.3b)
breadboards: 1

parts:
  Parça1 = Arduino Nano (Rev3.0)
  M1 = Dagu DGServo 9g (Pan and tilt) [part_number=RS001B]
  U1 = BUTTONPAD-4X4 [package=buttonpad-4x4-special]
  LCD1 = LCD screen

nets:
  GND: Parça1.GND, M1.gnd, LCD1.VSS
  N1: Parça1.D3, U1.G$2_RED
  N2: Parça1.D4, U1.G$3_GRN
  N3: Parça1.D5, U1.G$1_SIG2
  N4: Parça1.D9, M1.pulse
  5V: Parça1.5V, M1.vcc, LCD1.VDD
  N5: Parça1.A5, LCD1.RS
  N6: Parça1.A4, LCD1.V0
  N7: Parça1.A3, U1.G$4_GRN
  N8: Parça1.A2, U1.G$3_BLU
  N9: Parça1.A1, U1.G$3_GND
  N10: Parça1.A0, U1.G$3_RED

notes:
  GND
  Vcc
  SDA
  SCL
